// Digital circuit canis.dig as structural Verilog
module canis (
  input  clk
);

  ram #(.generic("addrBits := 16;")) ram_1 (
    .C(clk), ._1A({16{1'b0}}), ._1Din({32{1'b0}}), ._2A({16{1'b0}}), .we(1'b0), .am(2'b00), .sign(1'b0));  // open: _1D, _2D
endmodule
